// Logisim project Z80.circ as structural Verilog: 3 circuits, main circuit main
module main (
);

  Registers Main_Registers ();  // open: Data_In_8b, Select_Register, WE_Register, Data_In_16b, Select_Pair, WE_Pair, WE, LD_Register, CLK, R, LD_Pair, Data_Out_8b, Data_Out_16b
  Registers Alternate_Registers ();  // open: Data_In_8b, Select_Register, WE_Register, Data_In_16b, Select_Pair, WE_Pair, WE, LD_Register, CLK, R, LD_Pair, Data_Out_8b, Data_Out_16b
  Spec_Registers Special_Registers ();  // open: Data_In_8b, Select_Register, Data_In_16b, LD, WE, CLK, RST, out_8, out_9
endmodule

module Registers (
  input  [7:0] Data_In_8b,
  input  [2:0] Select_Register,
  input  WE_Register,
  input  [15:0] Data_In_16b,
  input  [1:0] Select_Pair,
  input  WE_Pair,
  input  WE,
  input  LD_Register,
  input  CLK,
  input  R,
  input  LD_Pair,
  output [7:0] Data_Out_8b,
  output [15:0] Data_Out_16b
);

  wire and_1_out, and_2_out, demultiplexer_1_out0, demultiplexer_1_out1, demultiplexer_1_out2,
       demultiplexer_1_out3, demultiplexer_2_out0, demultiplexer_2_out1, demultiplexer_2_out2,
       demultiplexer_2_out3, demultiplexer_2_out4, demultiplexer_2_out5, demultiplexer_2_out6,
       demultiplexer_2_out7, or_1_out, or_2_out, or_3_out, or_4_out, or_9_out, or_10_out, or_11_out,
       or_12_out;
  wire [7:0] C_q, E_q, F_q, L_q, multiplexer_1_out, or_5_out, or_6_out, or_7_out, or_8_out, or_13_out,
       or_14_out, or_15_out, or_16_out, pull_resistor_1_node;
  wire [15:0] multiplexer_2_out, pull_resistor_2_node;
  wire [15:8] A_q, B_q, D_q, H_q;

  Pull_Resistor pull_resistor_1 (.node(pull_resistor_1_node));
  assign pull_resistor_1_node = WE_Register ? Data_In_8b : 8'bz;  // Controlled_Buffer controlled_buffer_1
  Pull_Resistor pull_resistor_2 (.node(pull_resistor_2_node));
  assign pull_resistor_2_node = WE_Pair ? Data_In_16b : 16'bz;  // Controlled_Buffer controlled_buffer_2
  and and_1 (and_1_out, WE, WE_Pair);
  Demultiplexer #(.select(2)) demultiplexer_1 (
    .out0(demultiplexer_1_out0), .out1(demultiplexer_1_out1), .out2(demultiplexer_1_out2),
    .out3(demultiplexer_1_out3), .in(and_1_out), .sel(Select_Pair));
  and and_2 (and_2_out, WE, WE_Register);
  Demultiplexer #(.select(3)) demultiplexer_2 (
    .out0(demultiplexer_2_out0), .out1(demultiplexer_2_out1), .out2(demultiplexer_2_out2),
    .out3(demultiplexer_2_out3), .out4(demultiplexer_2_out4), .out5(demultiplexer_2_out5),
    .out6(demultiplexer_2_out6), .out7(demultiplexer_2_out7), .in(and_2_out), .sel(Select_Register));
  or or_1 (or_1_out, demultiplexer_2_out0, demultiplexer_1_out0);
  or or_2 (or_2_out, demultiplexer_2_out2, demultiplexer_1_out1);
  or or_3 (or_3_out, demultiplexer_2_out4, demultiplexer_1_out2);
  or or_4 (or_4_out, demultiplexer_2_out6, demultiplexer_1_out3);
  Register A (.D(or_5_out), .en(or_1_out), .clk(CLK), .Q(A_q), .clr(R));
  assign or_5_out = pull_resistor_1_node | pull_resistor_2_node[15:8];  // OR_Gate or_5, 8 bits wide
  Register B (.D(or_6_out), .en(or_2_out), .clk(CLK), .Q(B_q), .clr(R));
  assign or_6_out = pull_resistor_1_node | pull_resistor_2_node[15:8];  // OR_Gate or_6, 8 bits wide
  Register D (.D(or_7_out), .en(or_3_out), .clk(CLK), .Q(D_q), .clr(R));
  assign or_7_out = pull_resistor_1_node | pull_resistor_2_node[15:8];  // OR_Gate or_7, 8 bits wide
  Register H (.D(or_8_out), .en(or_4_out), .clk(CLK), .Q(H_q), .clr(R));
  assign or_8_out = pull_resistor_1_node | pull_resistor_2_node[15:8];  // OR_Gate or_8, 8 bits wide
  or or_9 (or_9_out, demultiplexer_2_out7, demultiplexer_1_out3);
  or or_10 (or_10_out, demultiplexer_2_out5, demultiplexer_1_out2);
  or or_11 (or_11_out, demultiplexer_2_out3, demultiplexer_1_out1);
  or or_12 (or_12_out, demultiplexer_2_out1, demultiplexer_1_out0);
  Register F (.D(or_13_out), .en(or_12_out), .clk(CLK), .Q(F_q), .clr(R));
  assign or_13_out = pull_resistor_1_node | pull_resistor_2_node[7:0];  // OR_Gate or_13, 8 bits wide
  Register C (.D(or_14_out), .en(or_11_out), .clk(CLK), .Q(C_q), .clr(R));
  assign or_14_out = pull_resistor_1_node | pull_resistor_2_node[7:0];  // OR_Gate or_14, 8 bits wide
  Register E (.D(or_15_out), .en(or_10_out), .clk(CLK), .Q(E_q), .clr(R));
  assign or_15_out = pull_resistor_1_node | pull_resistor_2_node[7:0];  // OR_Gate or_15, 8 bits wide
  Register L (.D(or_16_out), .en(or_9_out), .clk(CLK), .Q(L_q), .clr(R));
  assign or_16_out = pull_resistor_1_node | pull_resistor_2_node[7:0];  // OR_Gate or_16, 8 bits wide
  Multiplexer #(.select(3), .width(8)) multiplexer_1 (
    .in0(A_q), .in1(F_q), .in2(B_q), .in3(C_q), .in4(D_q), .in5(E_q), .in6(H_q), .in7(L_q),
    .out(multiplexer_1_out), .sel(Select_Register));
  Multiplexer #(.select(2), .width(16)) multiplexer_2 (
    .in0({A_q, F_q}), .in1({B_q, C_q}), .in2({D_q, E_q}), .in3({H_q, L_q}), .out(multiplexer_2_out),
    .sel(Select_Pair));
  assign Data_Out_8b = LD_Register ? multiplexer_1_out : 8'bz;  // Controlled_Buffer controlled_buffer_3
  assign Data_Out_16b = LD_Pair ? multiplexer_2_out : 16'bz;  // Controlled_Buffer controlled_buffer_4
  Pull_Resistor pull_resistor_3 (.node(Data_Out_8b));
  // Probe on Data_Out_8b
  Pull_Resistor pull_resistor_4 (.node(Data_Out_16b));
  // Probe on Data_Out_16b
endmodule

module Spec_Registers (
  input  [7:0] Data_In_8b,
  input  [2:0] Select_Register,
  input  [15:0] Data_In_16b,
  input  LD,
  input  WE,
  input  CLK,
  input  RST,
  output [7:0] out_8,
  output [15:0] out_9
);

  wire and_1_out, and_2_out, comparator_1_gt, demultiplexer_1_out0, demultiplexer_1_out1,
       demultiplexer_1_out2, demultiplexer_1_out3, demultiplexer_1_out4, demultiplexer_1_out5, not_1_out;
  wire [7:0] I_q, R_q;
  wire [15:0] IX_q, IY_q, multiplexer_1_out, PC_q, SP_q;

  Demultiplexer #(.select(3)) demultiplexer_1 (
    .out0(demultiplexer_1_out0), .out1(demultiplexer_1_out1), .out2(demultiplexer_1_out2),
    .out3(demultiplexer_1_out3), .out4(demultiplexer_1_out4), .out5(demultiplexer_1_out5), .in(WE),
    .sel(Select_Register));  // open: out6, out7
  Comparator #(.mode("unsigned"), .width(3)) comparator_1 (
    .a(Select_Register), .b(3'b001), .gt(comparator_1_gt));  // open: eq, lt
  not not_1 (not_1_out, comparator_1_gt);
  Register I (.D(Data_In_8b), .en(demultiplexer_1_out0), .clk(CLK), .Q(I_q), .clr(RST));
  Register R (.D(Data_In_8b), .en(demultiplexer_1_out1), .clk(CLK), .Q(R_q), .clr(RST));
  Register #(.width(16)) IX (.D(Data_In_16b), .en(demultiplexer_1_out2), .clk(CLK), .Q(IX_q), .clr(RST));
  Register #(.width(16)) IY (.D(Data_In_16b), .en(demultiplexer_1_out3), .clk(CLK), .Q(IY_q), .clr(RST));
  Register #(.width(16)) SP (.D(Data_In_16b), .en(demultiplexer_1_out4), .clk(CLK), .Q(SP_q), .clr(RST));
  Register #(.width(16)) PC (.D(Data_In_16b), .en(demultiplexer_1_out5), .clk(CLK), .Q(PC_q), .clr(RST));
  and and_1 (and_1_out, LD, comparator_1_gt);
  and and_2 (and_2_out, LD, not_1_out);
  Multiplexer #(.select(3), .width(16)) multiplexer_1 (
    .in0({{8{1'b0}}, I_q}), .in1({{8{1'b0}}, R_q}), .in2(IX_q), .in3(IY_q), .in4(SP_q), .in5(PC_q),
    .out(multiplexer_1_out), .sel(Select_Register));  // open: in6, in7
  Pull_Resistor pull_resistor_1 (.node(out_8));
  assign out_8 = and_2_out ? multiplexer_1_out[7:0] : 8'bz;  // Controlled_Buffer controlled_buffer_1
  assign out_9 = and_1_out ? multiplexer_1_out : 16'bz;  // Controlled_Buffer controlled_buffer_2
  Pull_Resistor pull_resistor_2 (.node(out_9));
endmodule
